# Fritzing sketch rpi-smart-thermometer-schematics (saved by Fritzing 0.9.6b)
breadboards: 1

parts:
  o1 = Module display OLED I2C 128x64 SSD1306 [package=THT]
  S1 = Momentary Switch [package=ksa_sealed_tac_switch]
  R1 = Resistor [tolerance=±5% resistance=220 package="0402 [SMD]"]
  MCU1 = Raspberry Pi Zero
  Part1 = DHT22 module  # not connected

nets:
  N1: o1.GND, R1.Pin_0, MCU1.pin_6, MCU1.pin_9
  N2: o1.VCC, MCU1.pin_1
  N3: o1.SCL, MCU1.pin_3
  N4: o1.SDA, MCU1.pin_5
  N5: S1.3, R1.Pin_1
  N6: S1.4, MCU1.pin_11

custom parts:
  Module display OLED I2C 128x64 SSD1306: Ecran OLED I2C SSD163 de 128x64 avec connexion I2C
